// Logisim project ebLab1and2.circ as structural Verilog: 1 circuit, main circuit main
module main (
  input  in_1,
  input  NOR_CIRCUIT,
  input  in_3,
  input  in_4,
  input  in_5,
  input  in_6,
  input  in_7,
  input  in_8,
  input  S1,
  input  S2,
  input  S3,
  input  S4,
  input  L1,
  input  L2,
  output out_15,
  output out_16,
  output out_17,
  output out_18,
  output out_19,
  output out_20
);

  wire and_3_out, and_4_out, and_5_out, and_6_out, and_7_out, and_8_out, and_9_out, and_10_out, nor_1_out,
       nor_2_out, nor_3_out, nor_4_out, nor_5_out, nor_6_out, nor_7_out, nor_8_out, nor_9_out, nor_10_out,
       nor_11_out, nor_12_out, not_1_out, not_2_out, not_3_out, not_4_out, not_5_out, not_6_out, not_7_out,
       not_8_out, not_9_out, not_10_out, not_11_out, not_12_out, not_13_out, not_14_out, or_1_out, or_2_out,
       or_3_out, or_4_out, or_5_out;

  not not_1 (not_1_out, in_5);
  not not_2 (not_2_out, in_6);
  not not_3 (not_3_out, in_7);
  not not_4 (not_4_out, S1);
  not not_5 (not_5_out, in_8);
  not not_6 (not_6_out, S2);
  not not_7 (not_7_out, S3);
  not not_8 (not_8_out, S4);
  or or_1 (or_1_out, in_5, in_8);
  or or_2 (or_2_out, not_3_out, not_5_out);
  or or_3 (or_3_out, not_1_out, not_5_out);
  or or_4 (or_4_out, in_7, not_5_out);
  or or_5 (or_5_out, not_3_out, in_8);
  nor nor_1 (nor_1_out, S1, S4);
  nor nor_2 (nor_2_out, not_7_out, not_8_out);
  nor nor_3 (nor_3_out, not_4_out, not_8_out);
  nor nor_4 (nor_4_out, S3, not_8_out);
  nor nor_5 (nor_5_out, not_7_out, S4);
  and and_1 (out_15, or_1_out, or_2_out, or_3_out, not_2_out);
  and and_2 (out_17, or_4_out, in_5, not_2_out, or_5_out);
  nor nor_6 (nor_6_out, nor_1_out, S2, nor_2_out, nor_3_out);
  nor nor_7 (nor_7_out, nor_4_out, not_4_out, S2, nor_5_out);
  not not_9 (not_9_out, L1);
  not not_10 (not_10_out, in_1);
  not not_11 (not_11_out, NOR_CIRCUIT);
  not not_12 (not_12_out, L2);
  not not_13 (not_13_out, in_4);
  not not_14 (not_14_out, in_3);
  and and_3 (and_3_out, nor_6_out, not_9_out, not_12_out);
  and and_4 (and_4_out, nor_6_out, not_9_out, L2);
  and and_5 (and_5_out, L1, not_12_out, not_9_out);
  and and_6 (and_6_out, L1, L2, not_12_out);
  and and_7 (and_7_out, nor_7_out, not_9_out, not_12_out);
  and and_8 (and_8_out, not_9_out, L2, not_12_out);
  and and_9 (and_9_out, nor_7_out, L1, not_12_out);
  and and_10 (and_10_out, L1, L2, not_9_out);
  nor nor_8 (nor_8_out, in_1, in_4);
  nor nor_9 (nor_9_out, not_14_out, not_13_out);
  nor nor_10 (nor_10_out, not_10_out, not_13_out);
  nor nor_11 (nor_11_out, in_3, not_13_out);
  nor nor_12 (nor_12_out, not_14_out, in_4);
  or or_6 (out_19, and_3_out, and_4_out, and_5_out, and_6_out);
  or or_7 (out_20, and_7_out, and_8_out, and_9_out, and_10_out);
  nor nor_13 (out_16, nor_8_out, NOR_CIRCUIT, nor_9_out, nor_10_out);
  nor nor_14 (out_18, nor_11_out, not_10_out, NOR_CIRCUIT, nor_12_out);

  // Notes on the sheet:
  //   OR AND CIRCUIT
  //   D1=1010, 0001
  //   D2=1011
  //   Both=1000
  //   00=normal
  //   01=D1 allowed
  //   10=D2 allowed
  //   11=Both locked
endmodule
