// Logisim project ebLab3.circ as structural Verilog: 1 circuit, main circuit main
module main (
  input  in_1,
  output out_2,
  output out_3,
  output out_4,
  output out_5,
  output out_6
);

  wire and_1_out, and_2_out, clock_1_out, not_1_out, not_2_out, not_3_out, not_4_out;

  Clock clock_1 (.out(clock_1_out));
  D_Flip_Flop d_ff_1 (.clk(clock_1_out), .D(in_1), .Q(out_2));  // open: Qn, preset, en, reset
  not not_1 (not_1_out, out_2);
  D_Flip_Flop d_ff_2 (.clk(clock_1_out), .D(out_2), .Q(out_3));  // open: Qn, preset, en, reset
  not not_2 (not_2_out, out_3);
  D_Flip_Flop d_ff_3 (.clk(clock_1_out), .D(out_3), .Q(out_4));  // open: Qn, preset, en, reset
  not not_3 (not_3_out, out_4);
  D_Flip_Flop d_ff_4 (.clk(clock_1_out), .D(out_4), .Q(out_5));  // open: Qn, preset, en, reset
  not not_4 (not_4_out, out_5);
  and and_1 (and_1_out, out_2, not_2_out, out_4, not_4_out);
  and and_2 (and_2_out, out_2, not_2_out, not_3_out, not_4_out);
  or or_1 (out_6, and_1_out, and_2_out);
endmodule
